// Logisim project 1. 기본게이트.circ as structural Verilog: 1 circuit, main circuit main
module main (
  input  A,
  input  A_2,
  input  A_3,
  input  Control,
  input  A_4,
  input  A_5,
  input  B,
  input  B_2,
  input  C,
  input  A_6,
  input  A_7,
  input  B_3,
  input  B_4,
  input  C_2,
  input  A_8,
  input  A_9,
  input  B_5,
  input  B_6,
  input  C_3,
  input  A_10,
  input  A_11,
  input  B_7,
  input  B_8,
  input  C_4,
  input  A_12,
  input  B_9,
  input  A_13,
  input  B_10,
  output F,
  output F_2,
  output F_3,
  output F_4,
  output F_5,
  output F_6,
  output F_7,
  output F_8,
  output F_9,
  output F_10,
  output F_11,
  output F_12,
  output F_13
);

  and and_1 (F_4, A_4, B_2);
  or or_1 (F_6, A_6, B_4);
  nand nand_1 (F_8, A_8, B_6);
  nor nor_1 (F_10, A_10, B_8);
  xor xor_1 (F_12, A_12, B_9);
  not not_1 (F, A);
  buf buffer_1 (F_2, A_2);
  assign F_3 = Control ? A_3 : 1'bz;  // Controlled_Buffer controlled_buffer_1
  xnor xnor_1 (F_13, A_13, B_10);
  and and_2 (F_5, A_5, B, C);
  or or_2 (F_7, A_7, B_3, C_2);
  nand nand_2 (F_9, A_9, B_5, C_3);
  nor nor_2 (F_11, A_11, B_7, C_4);

  // Notes on the sheet:
  //   AND 게이트
  //   OR 게이트
  //   NAND 게이트
  //   NOR 게이트
  //   XOR 게이트
  //   NOT 게이트
  //   버퍼 게이트
  //   3상태 버퍼 게이트
  //   XNOR 게이트
endmodule
