// Logisim project 2. ALU-Logic 파트.circ as structural Verilog: 1 circuit, main circuit main
module main (
  input  A,
  input  B,
  input  [1:0] in_3,
  input  A3,
  input  A2,
  input  A1,
  input  A0,
  input  B3,
  input  B2,
  input  B1,
  input  B0,
  input  [1:0] in_12,
  output F,
  output F3,
  output F2,
  output F1,
  output F0
);

  wire and_1_out, and_2_out, and_3_out, and_4_out, and_5_out, not_1_out, not_2_out, not_3_out, not_4_out,
       not_5_out, or_1_out, or_2_out, or_3_out, or_4_out, or_5_out, xor_1_out, xor_2_out, xor_3_out,
       xor_4_out, xor_5_out;

  or or_1 (or_1_out, A3, B3);
  and and_1 (and_1_out, A3, B3);
  xor xor_1 (xor_1_out, A3, B3);
  not not_1 (not_1_out, A3);
  Multiplexer #(.select(2), .enable("false")) multiplexer_1 (
    .in0(and_1_out), .in1(or_1_out), .in2(xor_1_out), .in3(not_1_out), .out(F3), .sel(in_12));
  and and_2 (and_2_out, A, B);
  or or_2 (or_2_out, A, B);
  xor xor_2 (xor_2_out, A, B);
  not not_2 (not_2_out, A);
  or or_3 (or_3_out, A2, B2);
  and and_3 (and_3_out, A2, B2);
  Multiplexer #(.select(2), .enable("false")) multiplexer_2 (
    .in0(and_2_out), .in1(or_2_out), .in2(xor_2_out), .in3(not_2_out), .out(F), .sel(in_3));
  xor xor_3 (xor_3_out, A2, B2);
  not not_3 (not_3_out, A2);
  Multiplexer #(.select(2), .enable("false")) multiplexer_3 (
    .in0(and_3_out), .in1(or_3_out), .in2(xor_3_out), .in3(not_3_out), .out(F2), .sel(in_12));
  and and_4 (and_4_out, A1, B1);
  or or_4 (or_4_out, A1, B1);
  not not_4 (not_4_out, A1);
  xor xor_4 (xor_4_out, A1, B1);
  Multiplexer #(.select(2), .enable("false")) multiplexer_4 (
    .in0(and_4_out), .in1(or_4_out), .in2(xor_4_out), .in3(not_4_out), .out(F1), .sel(in_12));
  or or_5 (or_5_out, A0, B0);
  and and_5 (and_5_out, A0, B0);
  not not_5 (not_5_out, A0);
  xor xor_5 (xor_5_out, A0, B0);
  Multiplexer #(.select(2), .enable("false")) multiplexer_5 (
    .in0(and_5_out), .in1(or_5_out), .in2(xor_5_out), .in3(not_5_out), .out(F0), .sel(in_12));

  // Notes on the sheet:
  //   00=AND, 01=OR, 10=XOR, 11=NOT
  //   00=AND, 01=OR, 10=XOR, 11=NOT
endmodule
