// Logisim project 3. ALU-감가산기 파트.circ as structural Verilog: 1 circuit, main circuit main
module main (
  input  A,
  input  A_2,
  input  B,
  input  B_2,
  input  A_3,
  input  Cin,
  input  B_3,
  input  A_4,
  input  B_4,
  input  Cin_2,
  input  A3,
  input  B3,
  input  A2,
  input  B2,
  input  A1,
  input  B1,
  input  A0,
  input  B0,
  input  \_0_가산__1_감산 ,
  input  A3_2,
  input  B3_2,
  input  A2_2,
  input  B2_2,
  input  A1_2,
  input  B1_2,
  input  A0_2,
  input  B0_2,
  output S,
  output S_2,
  output C,
  output C_2,
  output S_3,
  output S_4,
  output Cout,
  output Cout_2,
  output \오버플로 ,
  output S3,
  output S2,
  output S1,
  output S0,
  output \캐리 ,
  output \오버플로_2 ,
  output S3_2,
  output S2_2,
  output S1_2,
  output S0_2,
  output \캐리_2 
);

  wire adder_3_cout, adder_4_cout, adder_5_cout, adder_6_cout, adder_8_cout, adder_9_cout, and_1_out,
       and_2_out, and_4_out, and_5_out, not_1_out, not_2_out, xor_3_out, xor_4_out, xor_6_out, xor_8_out,
       xor_9_out;

  not not_1 (not_1_out, A);
  not not_2 (not_2_out, B);
  xor xor_1 (\오버플로 , \캐리 , adder_3_cout);
  xor xor_2 (\오버플로_2 , \캐리_2 , adder_4_cout);
  and and_1 (and_1_out, not_1_out, B);
  and and_2 (and_2_out, A, not_2_out);
  and and_3 (C_2, A, B);
  xor xor_3 (xor_3_out, A_3, B_3);
  and and_4 (and_4_out, A_3, B_3);
  Adder #(.width(1)) adder_1 (.a(B3), .b(A3), .out(S3), .cin(adder_3_cout), .cout(\캐리 ));
  xor xor_4 (xor_4_out, B3_2, \_0_가산__1_감산 );
  or or_1 (S_2, and_1_out, and_2_out);
  Adder #(.width(1)) adder_2 (.a(xor_4_out), .b(A3_2), .out(S3_2), .cin(adder_4_cout), .cout(\캐리_2 ));
  xor xor_5 (S_3, xor_3_out, Cin_2);
  and and_5 (and_5_out, xor_3_out, Cin_2);
  Adder #(.width(1)) adder_3 (.a(B2), .b(A2), .out(S2), .cin(adder_5_cout), .cout(adder_3_cout));
  xor xor_6 (xor_6_out, B2_2, \_0_가산__1_감산 );
  or or_2 (Cout, and_5_out, and_4_out);
  Adder #(.width(1)) adder_4 (.a(xor_6_out), .b(A2_2), .out(S2_2), .cin(adder_6_cout), .cout(adder_4_cout));
  xor xor_7 (S, A_2, B_2);
  and and_6 (C, A_2, B_2);
  xor xor_8 (xor_8_out, B1_2, \_0_가산__1_감산 );
  Adder #(.width(1)) adder_5 (.a(B1), .b(A1), .out(S1), .cin(adder_8_cout), .cout(adder_5_cout));
  Adder #(.width(1)) adder_6 (.a(xor_8_out), .b(A1_2), .out(S1_2), .cin(adder_9_cout), .cout(adder_6_cout));
  Adder #(.width(1)) adder_7 (.a(A_4), .b(B_4), .out(S_4), .cin(Cin), .cout(Cout_2));
  Adder #(.width(1)) adder_8 (.a(B0), .b(A0), .out(S0), .cin(1'b0), .cout(adder_8_cout));
  xor xor_9 (xor_9_out, B0_2, \_0_가산__1_감산 );
  Adder #(.width(1)) adder_9 (.a(xor_9_out), .b(A0_2), .out(S0_2), .cin(\_0_가산__1_감산 ), .cout(adder_9_cout));

  // Notes on the sheet:
  //   반가산기: HA, Half Adder
  //   전가산기: FA, Full Adder
  //   4비트 병렬가산기
  //   4비트 병렬감가산기
endmodule
