// Logisim project 4. ALU-비교기 파트.circ as structural Verilog: 3 circuits, main circuit main
module main (
  input  [3:0] A,
  input  [3:0] B,
  input  \입력_크다 ,
  input  \입력_작다 ,
  input  \입력_같다 ,
  output \출력_크다 ,
  output \출력_작다 ,
  output \출력_같다 
);

  wire \n1bit_비교기_1_출력_같다 , \n1bit_비교기_1_출력_작다 , \n1bit_비교기_1_출력_크다 , \n1bit_비교기_2_출력_같다 ,
       \n1bit_비교기_2_출력_작다 , \n1bit_비교기_2_출력_크다 , \n1bit_비교기_3_출력_같다 , \n1bit_비교기_3_출력_작다 ,
       \n1bit_비교기_3_출력_크다 ;

  \_1bit_비교기  \u_1bit_비교기_1  (
    .\입력_크다 (\입력_크다 ), .\입력_작다 (\입력_작다 ), .\입력_같다 (\입력_같다 ), .A(A[3]), .B(B[3]),
    .\출력_크다 (\n1bit_비교기_1_출력_크다 ), .\출력_작다 (\n1bit_비교기_1_출력_작다 ), .\출력_같다 (\n1bit_비교기_1_출력_같다 ));
  \_1bit_비교기  \u_1bit_비교기_2  (
    .\입력_크다 (\n1bit_비교기_1_출력_크다 ), .\입력_작다 (\n1bit_비교기_1_출력_작다 ), .\입력_같다 (\n1bit_비교기_1_출력_같다 ), .A(A[2]),
    .B(B[2]), .\출력_크다 (\n1bit_비교기_2_출력_크다 ), .\출력_작다 (\n1bit_비교기_2_출력_작다 ), .\출력_같다 (\n1bit_비교기_2_출력_같다 ));
  \_1bit_비교기  \u_1bit_비교기_3  (
    .\입력_크다 (\n1bit_비교기_2_출력_크다 ), .\입력_작다 (\n1bit_비교기_2_출력_작다 ), .\입력_같다 (\n1bit_비교기_2_출력_같다 ), .A(A[1]),
    .B(B[1]), .\출력_크다 (\n1bit_비교기_3_출력_크다 ), .\출력_작다 (\n1bit_비교기_3_출력_작다 ), .\출력_같다 (\n1bit_비교기_3_출력_같다 ));
  \_1bit_비교기  \u_1bit_비교기_4  (
    .\입력_크다 (\n1bit_비교기_3_출력_크다 ), .\입력_작다 (\n1bit_비교기_3_출력_작다 ), .\입력_같다 (\n1bit_비교기_3_출력_같다 ), .A(A[0]),
    .B(B[0]), .\출력_크다 (\출력_크다 ), .\출력_작다 (\출력_작다 ), .\출력_같다 (\출력_같다 ));

  // Notes on the sheet:
  //   입력_같다의 초기치는 1
endmodule

module \_1bit_비교기  (
  input  A,
  input  B,
  input  \입력_크다 ,
  input  \입력_작다 ,
  input  \입력_같다 ,
  output \출력_크다 ,
  output \출력_작다 ,
  output \출력_같다 
);

  wire and_1_out, and_2_out, xnor_1_out;

  xnor xnor_1 (xnor_1_out, A, B);
  and and_1 (and_1_out, \입력_같다 , A, ~B);  // AND_Gate
  and and_2 (and_2_out, \입력_같다 , B, ~A);  // AND_Gate
  or or_1 (\출력_크다 , and_1_out, \입력_크다 );
  or or_2 (\출력_작다 , and_2_out, \입력_작다 );
  and and_3 (\출력_같다 , xnor_1_out, \입력_같다 );

  // Notes on the sheet:
  //   입력_같다의 초기치는 1
endmodule

module \_4bit_비교기  (
  input  [3:0] A,
  input  [3:0] B,
  input  \입력_크다 ,
  input  \입력_작다 ,
  input  \입력_같다 ,
  output \출력_크다 ,
  output \출력_작다 ,
  output \출력_같다 
);

  wire \n1bit_비교기_1_출력_같다 , \n1bit_비교기_1_출력_작다 , \n1bit_비교기_1_출력_크다 , \n1bit_비교기_2_출력_같다 ,
       \n1bit_비교기_2_출력_작다 , \n1bit_비교기_2_출력_크다 , \n1bit_비교기_3_출력_같다 , \n1bit_비교기_3_출력_작다 ,
       \n1bit_비교기_3_출력_크다 ;

  \_1bit_비교기  \u_1bit_비교기_1  (
    .\입력_크다 (\입력_크다 ), .\입력_작다 (\입력_작다 ), .\입력_같다 (\입력_같다 ), .A(A[3]), .B(B[3]),
    .\출력_크다 (\n1bit_비교기_1_출력_크다 ), .\출력_작다 (\n1bit_비교기_1_출력_작다 ), .\출력_같다 (\n1bit_비교기_1_출력_같다 ));
  \_1bit_비교기  \u_1bit_비교기_2  (
    .\입력_크다 (\n1bit_비교기_1_출력_크다 ), .\입력_작다 (\n1bit_비교기_1_출력_작다 ), .\입력_같다 (\n1bit_비교기_1_출력_같다 ), .A(A[2]),
    .B(B[2]), .\출력_크다 (\n1bit_비교기_2_출력_크다 ), .\출력_작다 (\n1bit_비교기_2_출력_작다 ), .\출력_같다 (\n1bit_비교기_2_출력_같다 ));
  \_1bit_비교기  \u_1bit_비교기_3  (
    .\입력_크다 (\n1bit_비교기_2_출력_크다 ), .\입력_작다 (\n1bit_비교기_2_출력_작다 ), .\입력_같다 (\n1bit_비교기_2_출력_같다 ), .A(A[1]),
    .B(B[1]), .\출력_크다 (\n1bit_비교기_3_출력_크다 ), .\출력_작다 (\n1bit_비교기_3_출력_작다 ), .\출력_같다 (\n1bit_비교기_3_출력_같다 ));
  \_1bit_비교기  \u_1bit_비교기_4  (
    .\입력_크다 (\n1bit_비교기_3_출력_크다 ), .\입력_작다 (\n1bit_비교기_3_출력_작다 ), .\입력_같다 (\n1bit_비교기_3_출력_같다 ), .A(A[0]),
    .B(B[0]), .\출력_크다 (\출력_크다 ), .\출력_작다 (\출력_작다 ), .\출력_같다 (\출력_같다 ));

  // Notes on the sheet:
  //   입력_같다의 초기치는 1
endmodule
