// Logisim project 5. 8bit ALU.circ as structural Verilog: 5 circuits, main circuit main
module main (
  input  _8b,
  input  _7b,
  input  _6b,
  input  _5b,
  input  _4b,
  input  _3b,
  input  _2b,
  input  _1b,
  input  _8b_2,
  input  _7b_2,
  input  _6b_2,
  input  _5b_2,
  input  _4b_2,
  input  _3b_2,
  input  _2b_2,
  input  _1b_2,
  input  INC,
  input  _2_complement,
  input  ADD,
  input  SUB,
  output CarryFlag,
  output OverFlow,
  output ZeroFlag,
  output SignFlag
);

  wire multiplexer_1_out, multiplexer_2_out, nor_1_out, not_1__1b_2, not_1__2b_2, not_1__3b_2, not_1__4b_2,
       not_1__5b_2, not_1__6b_2, not_1__7b_2, not_1__8b_2, not_2__1b_2, not_2__2b_2, not_2__3b_2,
       not_2__4b_2, not_2__5b_2, not_2__6b_2, not_2__7b_2, not_2__8b_2, not_3_out, or_1_out, zero_1__1b_2,
       zero_1__2b_2, zero_1__3b_2, zero_1__4b_2, zero_1__5b_2, zero_1__6b_2, zero_1__7b_2, zero_1__8b_2;
  wire [3:0] n8bitadder_1__1b_3, n8bitadder_1__5b_3;

  or or_1 (or_1_out, _2_complement, INC);
  nor nor_1 (nor_1_out, SUB, ADD, _2_complement, INC);
  Hex_Digit_Display hex_digit_display_1 (.value({_8b, _7b, _6b, _5b}));  // open: dp
  Hex_Digit_Display hex_digit_display_2 (.value({_4b, _3b, _2b, _1b}));  // open: dp
  Hex_Digit_Display hex_digit_display_3 (.value(n8bitadder_1__5b_3));  // open: dp
  Hex_Digit_Display hex_digit_display_4 (.value(n8bitadder_1__1b_3));  // open: dp
  Hex_Digit_Display hex_digit_display_5 (.value({_8b_2, _7b_2, _6b_2, _5b_2}));  // open: dp
  Hex_Digit_Display hex_digit_display_6 (.value({_4b_2, _3b_2, _2b_2, _1b_2}));  // open: dp
  Zero zero_1 (
    .select(or_1_out), ._8b(_8b), ._7b(_7b), ._6b(_6b), ._5b(_5b), ._4b(_4b), ._3b(_3b), ._2b(_2b),
    ._1b(_1b), ._8b_2(zero_1__8b_2), ._7b_2(zero_1__7b_2), ._6b_2(zero_1__6b_2), ._5b_2(zero_1__5b_2),
    ._4b_2(zero_1__4b_2), ._3b_2(zero_1__3b_2), ._2b_2(zero_1__2b_2), ._1b_2(zero_1__1b_2));
  Not not_1 (
    .select(_2_complement), ._8b(_8b_2), ._7b(_7b_2), ._6b(_6b_2), ._5b(_5b_2), ._4b(_4b_2), ._3b(_3b_2),
    ._2b(_2b_2), ._1b(_1b_2), ._8b_2(not_1__8b_2), ._7b_2(not_1__7b_2), ._6b_2(not_1__6b_2),
    ._5b_2(not_1__5b_2), ._4b_2(not_1__4b_2), ._3b_2(not_1__3b_2), ._2b_2(not_1__2b_2), ._1b_2(not_1__1b_2));
  Not not_2 (
    .select(SUB), ._8b(not_1__8b_2), ._7b(not_1__7b_2), ._6b(not_1__6b_2), ._5b(not_1__5b_2),
    ._4b(not_1__4b_2), ._3b(not_1__3b_2), ._2b(not_1__2b_2), ._1b(not_1__1b_2), ._8b_2(not_2__8b_2),
    ._7b_2(not_2__7b_2), ._6b_2(not_2__6b_2), ._5b_2(not_2__5b_2), ._4b_2(not_2__4b_2), ._3b_2(not_2__3b_2),
    ._2b_2(not_2__2b_2), ._1b_2(not_2__1b_2));
  _8BitAdder u_8bitadder_1 (
    .CarryFlag(CarryFlag), .OverFlow(OverFlow), .ZeroFlag(ZeroFlag), .SignFlag(SignFlag), ._8b(zero_1__8b_2),
    ._7b(zero_1__7b_2), ._6b(zero_1__6b_2), ._5b(zero_1__5b_2), ._4b(zero_1__4b_2), ._3b(zero_1__3b_2),
    ._2b(zero_1__2b_2), ._1b(zero_1__1b_2), ._8b_2(not_2__8b_2), ._7b_2(not_2__7b_2), ._6b_2(not_2__6b_2),
    ._5b_2(not_2__5b_2), ._4b_2(not_2__4b_2), ._3b_2(not_2__3b_2), ._2b_2(not_2__2b_2), ._1b_2(not_2__1b_2),
    ._8b_3(n8bitadder_1__5b_3[3]), ._7b_3(n8bitadder_1__5b_3[2]), ._6b_3(n8bitadder_1__5b_3[1]),
    ._5b_3(n8bitadder_1__5b_3[0]), ._4b_3(n8bitadder_1__1b_3[3]), ._3b_3(n8bitadder_1__1b_3[2]),
    ._2b_3(n8bitadder_1__1b_3[1]), ._1b_3(n8bitadder_1__1b_3[0]), ._0_or_1(multiplexer_1_out),
    .select(nor_1_out));  // open: x
  Multiplexer #(.enable("false")) multiplexer_1 (
    .in0(multiplexer_2_out), .in1(not_3_out), .out(multiplexer_1_out), .sel(nor_1_out));
  not not_3 (not_3_out, multiplexer_2_out);
  Multiplexer #(.enable("false")) multiplexer_2 (.in0(1'b1), .in1(1'b0), .out(multiplexer_2_out), .sel(ADD));

  // Notes on the sheet:
  //   R1
  //   ADD R0, R1, R2	; R0  R1 + R2 
  //   SUB R0, R1, R2	; R0  R1 - R2 
  //   INC   R2                ; R0  R2 + 1 
  //   2’s Complement	; R0  ~R2 + 1 
  //   R0
  //   R2
  //   plus 1
  //   Select
endmodule

module Not (
  input  _8b,
  input  _7b,
  input  _6b,
  input  _5b,
  input  _4b,
  input  _3b,
  input  _2b,
  input  _1b,
  input  select,
  output _8b_2,
  output _7b_2,
  output _6b_2,
  output _5b_2,
  output _4b_2,
  output _3b_2,
  output _2b_2,
  output _1b_2
);

  wire not_1_out, not_2_out, not_3_out, not_4_out, not_5_out, not_6_out, not_7_out, not_8_out;

  not not_1 (not_1_out, _8b);
  Multiplexer #(.enable("false")) multiplexer_1 (.in0(_8b), .in1(not_1_out), .out(_8b_2), .sel(select));
  not not_2 (not_2_out, _7b);
  Multiplexer #(.enable("false")) multiplexer_2 (.in0(_6b), .in1(not_4_out), .out(_6b_2), .sel(select));
  Multiplexer #(.enable("false")) multiplexer_3 (.in0(_7b), .in1(not_2_out), .out(_7b_2), .sel(select));
  not not_3 (not_3_out, _5b);
  not not_4 (not_4_out, _6b);
  Multiplexer #(.enable("false")) multiplexer_4 (.in0(_5b), .in1(not_3_out), .out(_5b_2), .sel(select));
  not not_5 (not_5_out, _4b);
  Multiplexer #(.enable("false")) multiplexer_5 (.in0(_4b), .in1(not_5_out), .out(_4b_2), .sel(select));
  not not_6 (not_6_out, _3b);
  Multiplexer #(.enable("false")) multiplexer_6 (.in0(_2b), .in1(not_7_out), .out(_2b_2), .sel(select));
  Multiplexer #(.enable("false")) multiplexer_7 (.in0(_3b), .in1(not_6_out), .out(_3b_2), .sel(select));
  not not_7 (not_7_out, _2b);
  not not_8 (not_8_out, _1b);
  Multiplexer #(.enable("false")) multiplexer_8 (.in0(_1b), .in1(not_8_out), .out(_1b_2), .sel(select));

  // Notes on the sheet:
  //   Not
endmodule

// FAdd
module FullAdder (
  input  A,
  input  B,
  input  carry_in,
  output carry_out,
  output sum
);

  wire and_1_out, and_2_out, xor_1_out;

  and and_1 (and_1_out, A, B);
  and and_2 (and_2_out, carry_in, xor_1_out);
  or or_1 (carry_out, and_1_out, and_2_out);
  xor xor_1 (xor_1_out, A, B);
  xor xor_2 (sum, carry_in, xor_1_out);

  // Notes on the sheet:
  //   FullAdder
endmodule

module _8BitAdder (
  input  _8b,
  input  _7b,
  input  _6b,
  input  _5b,
  input  _4b,
  input  _3b,
  input  _2b,
  input  _1b,
  input  x,
  input  _8b_2,
  input  _7b_2,
  input  _6b_2,
  input  _5b_2,
  input  _4b_2,
  input  _3b_2,
  input  _2b_2,
  input  _1b_2,
  input  _0_or_1,
  input  select,
  output CarryFlag,
  output OverFlow,
  output ZeroFlag,
  output SignFlag,
  output _8b_3,
  output _7b_3,
  output _6b_3,
  output _5b_3,
  output _4b_3,
  output _3b_3,
  output _2b_3,
  output _1b_3
);

  wire fulladder_1_carry_out, fulladder_3_carry_out, fulladder_4_carry_out, fulladder_5_carry_out,
       fulladder_6_carry_out, fulladder_7_carry_out, fulladder_8_carry_out, not_1_out, not_2_out, or_1_out;

  xor xor_1 (OverFlow, fulladder_1_carry_out, CarryFlag);
  and and_1 (ZeroFlag, not_2_out, not_1_out);
  not not_1 (not_1_out, or_1_out);
  or or_1 (or_1_out, _1b_3, _2b_3, _3b_3, _4b_3, _5b_3, _6b_3, _7b_3, _8b_3);
  FullAdder fulladder_1 (
    .A(_7b), .B(_7b_2), .carry_in(fulladder_3_carry_out), .carry_out(fulladder_1_carry_out), .sum(_7b_3));
  FullAdder fulladder_2 (.A(_8b), .B(_8b_2), .carry_in(fulladder_1_carry_out), .carry_out(CarryFlag), .sum(_8b_3));
  FullAdder fulladder_3 (
    .A(_6b), .B(_6b_2), .carry_in(fulladder_5_carry_out), .carry_out(fulladder_3_carry_out), .sum(_6b_3));
  FullAdder fulladder_4 (
    .A(_4b), .B(_4b_2), .carry_in(fulladder_7_carry_out), .carry_out(fulladder_4_carry_out), .sum(_4b_3));
  FullAdder fulladder_5 (
    .A(_5b), .B(_5b_2), .carry_in(fulladder_4_carry_out), .carry_out(fulladder_5_carry_out), .sum(_5b_3));
  FullAdder fulladder_6 (
    .A(_2b), .B(_2b_2), .carry_in(fulladder_8_carry_out), .carry_out(fulladder_6_carry_out), .sum(_2b_3));
  FullAdder fulladder_7 (
    .A(_3b), .B(_3b_2), .carry_in(fulladder_6_carry_out), .carry_out(fulladder_7_carry_out), .sum(_3b_3));
  FullAdder fulladder_8 (.A(_1b), .B(_1b_2), .carry_in(_0_or_1), .carry_out(fulladder_8_carry_out), .sum(_1b_3));
  not not_2 (not_2_out, select);

  assign SignFlag = _8b_3;

  // Notes on the sheet:
  //   8BitAdder
  //   8bitAdder
endmodule

module Zero (
  input  _8b,
  input  _7b,
  input  _6b,
  input  _5b,
  input  _4b,
  input  _3b,
  input  _2b,
  input  _1b,
  input  select,
  output _8b_2,
  output _7b_2,
  output _6b_2,
  output _5b_2,
  output _4b_2,
  output _3b_2,
  output _2b_2,
  output _1b_2
);

  Multiplexer #(.enable("false")) multiplexer_1 (.in0(_7b), .in1(1'b0), .out(_7b_2), .sel(select));
  Multiplexer #(.enable("false")) multiplexer_2 (.in0(_8b), .in1(1'b0), .out(_8b_2), .sel(select));
  Multiplexer #(.enable("false")) multiplexer_3 (.in0(_6b), .in1(1'b0), .out(_6b_2), .sel(select));
  Multiplexer #(.enable("false")) multiplexer_4 (.in0(_5b), .in1(1'b0), .out(_5b_2), .sel(select));
  Multiplexer #(.enable("false")) multiplexer_5 (.in0(_3b), .in1(1'b0), .out(_3b_2), .sel(select));
  Multiplexer #(.enable("false")) multiplexer_6 (.in0(_4b), .in1(1'b0), .out(_4b_2), .sel(select));
  Multiplexer #(.enable("false")) multiplexer_7 (.in0(_2b), .in1(1'b0), .out(_2b_2), .sel(select));
  Multiplexer #(.enable("false")) multiplexer_8 (.in0(_1b), .in1(1'b0), .out(_1b_2), .sel(select));

  // Notes on the sheet:
  //   Zero
endmodule
